# Fritzing sketch Outdoor Watering System Schematic (saved by Fritzing 0.9.3b)

parts:
  Part1 = Arduino Mega 2560 (Rev3)
  Part2 = Soil Moisture Sensor
  Power_plug1 = Power plug  # not connected
  M1 = DC Motor  # not connected
  Power_plug2 = Power plug
  K1 = Relay [part_number=FRS1B-S package=THT]

nets:
  N1: Part1.D8_PWM, Part2.SIG
  5V: Part1.5V, Part2.VCC
  GND: Part1.GND, Part2.GND
  N2: Power_plug2.VCC, K1.C2

notes:
  12V Water Valve
  5V Power Source
  12V Power Source
